# Fritzing sketch basic_schematic (saved by Fritzing 0.9.3b)
breadboards: 1

parts:
  AKC5951(55) = SI4735-D60 [package=SSOP]
  Y1 = CRYSTAL [package=tc26h]
  C1 = Capacitor [part_number=22pF package=cap-pth-small2]
  C2 = Capacitor [part_number=22pF package=cap-pth-small2]
  R1 = Resistor [tolerance=±5% resistance=10k package=THT]
  LED1 = LEDs [package=led10mm]
  Pro_Mini_3_3v_8MHz = Arduino Pro Mini (3.3V)
  C3 = Electrolytic Capacitor [capacitance=470µF package="200 mil [THT, electrolytic]"]
  C4 = Capacitor [part_number=1nF package=cap-pth-small2]
  U1 = 2.5mm Audio Jack [part_number=Audio package=stereojack2.5mm_smd]
  R2 = Resistor [tolerance=±5% resistance=22k package=THT]
  R3 = Resistor [tolerance=±5% resistance=4.7k package=THT]
  C5 = Capacitor [part_number=100nF package=cap-pth-small2]
  L1 = Inductor [package="400 mil [THT]"]
  C6 = Capacitor [part_number=100pF package=cap-pth-small2]
  C7 = Capacitor [part_number=3nF package=cap-pth-small2]
  C8 = Capacitor [part_number=100nF package=cap-pth-small2]
  C9 = Electrolytic Capacitor [capacitance=22µF package="200 mil [THT, electrolytic]"]

nets:
  N1: AKC5951(55).DOUT, Y1.2, C1.2
  N2: AKC5951(55).DFS, Y1.1, C2.2
  GND: AKC5951(55).GPO3, AKC5951(55).AMI, AKC5951(55).SCLK, AKC5951(55).VA, AKC5951(55).LOUT, C1.1, C2.1, LED1.C, Pro_Mini_3_3v_8MHz.GND, C3.-, C4.2, R2.Pin_1, C5.2, C8.2, C9.-
  N3: AKC5951(55).GPO2, LED1.A
  RESET: AKC5951(55).GPO1, R1.Pin_1, Pro_Mini_3_3v_8MHz.RESET
  N4: AKC5951(55).NC#5, Pro_Mini_3_3v_8MHz.A5
  N5: AKC5951(55).NC#6, Pro_Mini_3_3v_8MHz.A4
  N6: AKC5951(55).NC#9, R1.Pin_0, C3.+, C4.1
  N7: AKC5951(55).NC#10, U1.LEFT
  N8: AKC5951(55).GND#12, U1.RIGHT
  N9: AKC5951(55).GND#13, R3.Pin_0
  N10: AKC5951(55).RST, R2.Pin_0, R3.Pin_1
  3.3V: AKC5951(55).SEN, Pro_Mini_3_3v_8MHz.VCC, C5.1
  N11: AKC5951(55).SDIO, L1.pin_1
  N12: AKC5951(55).RCLK, L1.pin_0
  N13: AKC5951(55).VD, C7.1
  N14: AKC5951(55).DBYP, C6.1
  N15: AKC5951(55).ROUT, C8.1, C9.+
  Antenna: C6.2, C7.2

notes:
  SDA / SDIO
  SCL / SCLK
  AM Ferrite Antenna
  FM / SW  Antenna
